# Fritzing sketch simpleLED (saved by Fritzing 0.9.3b)
breadboards: 1

parts:
  LED = LED - 3mm [color="Red (633nm)" package="3 mm [THT]"]
  Bauteil3 = Adafruit T-Cobbler Plus [part_number="Adafruit #1989 and #2028"]
  part = Resistor [tolerance=±5% resistance=1k package=THT]

nets:
  N1: LED.cathode, part.Pin_0
  N2: LED.anode, Bauteil3.GND
  N3: Bauteil3.GPIO26, part.Pin_1

custom parts:
  Adafruit T-Cobbler Plus: The Raspberry Pi has landed on the Maker World like a 40-GPIO pinned, quad-USB ported, credit card sized bomb of DIY joy. And while you can use most of our great Model B accessories by hooking up our downgrade cable, its probably a good time to upgrade your set up and accessorize using all of the 40 pins. That's why we now carry the Assembled Adafruit Pi T-Cobbler Plus - Breakout + Cable for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
